# Fritzing sketch distance_mesure (saved by Fritzing 0.9.0b)
circuit board: 8.46667cm x 5.64444cm
breadboards: 1

parts:
  UNO = Arduino Uno (Rev3)
  R1 = Trimmer Potentiometer [maximum_resistance=10kΩ package=THT]
  V1 = DC Power [voltage=5]
  V2 = DC Power [voltage=3.3]
  1602A = LCD-16X2 [package=lcd-16x2]
  HC-SR04 = SRF05 Ultrasonic Rangefinder

nets:
  N1: UNO.D8, HC-SR04.Trig
  N2: UNO.D11_PWM/MOSI, 1602A.E
  N3: UNO.D12/MISO, 1602A.RS
  GND: UNO.GND, R1.leg1, V1.V-, V2.V-, 1602A.VSS, 1602A.R_W, 1602A.K, HC-SR04.GND
  N4: UNO.D2, 1602A.DB7
  N5: UNO.D3_PWM, 1602A.DB6
  N6: UNO.D4, 1602A.DB5
  N7: UNO.D5_PWM, 1602A.DB4
  N8: UNO.D7, HC-SR04.Echo
  5V: UNO.5V, R1.leg2, V1.V+, 1602A.VDD, HC-SR04.VCC
  N9: R1.wiper, 1602A.VO
  N10: V2.V+, 1602A.A
