# Fritzing sketch FlowerMonitors (saved by Fritzing 0.9.1b)
breadboards: 1

parts:
  Part1 = Arduino Uno (Rev3)
  LCD1 = LCD screen
  R1 = Trimmer Potentiometer [maximum_resistance=10kΩ package=THT]
  R2 = Photocell (LDR) [package=THT]
  R3 = Resistor [tolerance=±5% resistance=220 package=THT]
  VCC1 = 4 x AAA Battery Mount
  R4 = Resistor [tolerance=±5% resistance=220 package=THT]
  C1 = Electrolytic Capacitor [capacitance=22µF package="100 mil [THT, electrolytic]"]
  IC1 = IC, DIP package, 16 pins [chip_label=LM324N]
  VCC2 = Battery block 9V
  U1 = mystery part, 4 pins [chip_label="M Sens"]

nets (from the schematic view):
  N1: Part1.A0, U1.pin4
  N2: Part1.A1, R2.pin_0, R3.Pin_1
  N3: Part1.D9_PWM, R4.Pin_1
  GND: Part1.GND, LCD1.R/W, VCC1.-
  N4: Part1.D2, LCD1.DB7
  N5: Part1.D3_PWM, LCD1.DB6
  N6: Part1.D4, LCD1.DB5
  N7: Part1.D5_PWM, LCD1.DB4
  N8: Part1.D6_PWM, LCD1.E
  N9: Part1.D7, LCD1.RS
  N10: LCD1.VSS, LCD1.LED-, R1.leg1, R2.pin_1, C1.-, IC1.pin13, VCC2.-, U1.pin2
  N11: LCD1.VDD, R1.leg2
  N12: LCD1.V0, R1.wiper
  N13: LCD1.LED+, IC1.pin1, IC1.pin2
  N14: R3.Pin_0, VCC1.+, U1.pin1
  N15: R4.Pin_0, C1.+, IC1.pin3
  N16: IC1.pin4, VCC2.+
