# Fritzing sketch PlantMonitor (saved by Fritzing 0.9.1b)
breadboards: 1

parts:
  Atmel_328 = Arduino Uno (Rev3)
  16x2 = LCD screen
  R2 = Photocell (LDR) [package=THT]
  R3 = Resistor [tolerance=±5% resistance=10k package=THT]
  R4 = Resistor [tolerance=±5% resistance=220 package=THT]
  C1 = Electrolytic Capacitor [capacitance=22µF package="100 mil [THT, electrolytic]"]
  R5 = Trimmer Potentiometer [maximum_resistance=10kΩ package=THT]
  R6 = Trimmer Potentiometer [maximum_resistance=10kΩ package=THT]
  R1 = Trimmer Potentiometer [maximum_resistance=10kΩ package=THT]
  LED1 = LED - 5mm [color="Red (633nm)" package="5 mm [THT]"]
  R7 = Resistor [tolerance=±5% resistance=220 package=THT]
  LM358 = LM358 [package=dip08]
  2N3906 = PNP-Transistor [package="TO92 [THT]"]
  R8 = Resistor [tolerance=±5% resistance=1k package=THT]
  R9 = Resistor [tolerance=±5% resistance=100k package=THT]
  R10 = Resistor [tolerance=±5% resistance=20k package=THT]
  MOISTURE_SENSOR = Header 2 [package=springterminal-2.54mm-2]
  2N3904 = TRANSISTOR_NPN_2 [package=to-92]
  R11 = Resistor [tolerance=±5% resistance=1k package=THT]
  LED2 = LED - 5mm [color="Red (633nm)" package="5 mm [THT]"]
  R12 = Resistor [tolerance=±5% resistance=220 package=THT]
  R13 = Resistor [tolerance=±5% resistance=1k package=THT]
  2N3907 = PNP-Transistor [package="TO92 [THT]"]
  R14 = Trimmer Potentiometer [maximum_resistance=10kΩ package=THT]

nets:
  N1: Atmel_328.A0, R10.Pin_0, MOISTURE_SENSOR.2
  N2: Atmel_328.A1, R3.Pin_0
  N3: Atmel_328.A2, R5.wiper
  N4: Atmel_328.A3, R6.wiper
  N5: Atmel_328.D8, R8.Pin_0, R13.Pin_0
  N6: Atmel_328.D9_PWM, R4.Pin_1
  N7: Atmel_328.D10_PWM/SS, R11.Pin_0
  GND: Atmel_328.GND, 16x2.VSS, 16x2.R/W, 16x2.LED-, R2.pin_1, C1.-, R5.leg1, R6.leg1, R1.leg1, LM358.G$1_V-, 2N3904.E, R12.Pin_0, R14.wiper
  N8: Atmel_328.D2, 16x2.DB7
  N9: Atmel_328.D3_PWM, 16x2.DB6
  N10: Atmel_328.D4, 16x2.DB5
  N11: Atmel_328.D5_PWM, 16x2.DB4
  N12: Atmel_328.D6_PWM, 16x2.E
  N13: Atmel_328.D7, 16x2.RS
  5V: Atmel_328.5V, 16x2.VDD, R3.Pin_1, R5.leg2, R6.leg2, R1.leg2, LED1.anode, 2N3906.E, R9.Pin_1, 2N3907.E
  N14: 16x2.V0, R1.wiper
  N15: 16x2.LED+, LM358.G$1_OUT, LM358.G$1_-IN
  N16: R4.Pin_0, C1.+, LM358.G$1_+IN
  N17: LED1.cathode, R7.Pin_0
  N18: R7.Pin_1, 2N3904.C
  9V: LM358.G$1_V+
  N19: 2N3906.B, R8.Pin_1, R9.Pin_0
  N20: 2N3906.C, MOISTURE_SENSOR.1
  N21: R10.Pin_1, R14.leg1
  N22: 2N3904.B, R11.Pin_1
  N23: LED2.cathode, R12.Pin_1
  N24: LED2.anode, 2N3907.C
  N25: R13.Pin_1, 2N3907.B

notes:
  Connect MOISTURE SENSOR directly to probe, like two galvanized nails on the extension cord.
